# Fritzing sketch MusiqueBox (saved by Fritzing 0.9.3b)
breadboards: 1

parts:
  J1 = STM32 Nucleo boards
  S1 = Pushbutton [package="[THT]"]
  S2 = Pushbutton [package="[THT]"]
  S3 = Pushbutton [package="[THT]"]
  R1 = Rotary Potentiometer (Small) [maximum_resistance=100kΩ package=THT]
  R2 = Rotary Potentiometer (Small) [maximum_resistance=100kΩ package=THT]
  R3 = Resistor [tolerance=±5% resistance=220 package=THT]
  R4 = Resistor [tolerance=±5% resistance=220 package=THT]
  J2 = female pin header, 3 pins [form="♀ (female)"]
  J4 = female pin header, 3 pins [form="♀ (female)"]
  IC1 = Dual Op-Amp [package=dip08]
  R5 = Trimmer Potentiometer [maximum_resistance=10kΩ package=THT]
  R6 = Trimmer Potentiometer [maximum_resistance=10kΩ package=THT]
  R7 = Resistor [tolerance=±5% resistance=10k package=THT]
  R8 = Resistor [tolerance=±5% resistance=10k package=THT]

nets (from the schematic view):
  N1: J1.A2, IC1.A_+IN
  N2: J1.A4/SDA, R2.wiper
  N3: J1.A5/SCL, R1.wiper
  N4: J1.SWO, R1.leg2, R2.leg2
  N5: J1.D8, S2.Pin_1, S2.Pin_2
  N6: J1.D11_PWM/MOSI, S1.Pin_1, S1.Pin_2
  N7: J1.D12/MISO, J4.pin3
  N8: J1.D13/SCK, IC1.B_+IN
  N9: J1.D7, S3.Pin_1, S3.Pin_2
  N10: J1.3V3, R3.Pin_1, R4.Pin_1
  N11: J1.GND, S1.Pin_3, S1.Pin_4, S2.Pin_3, S2.Pin_4, S3.Pin_3, S3.Pin_4, J2.pin2, R7.Pin_0, R8.Pin_1
  N12: R1.leg1, R4.Pin_0
  N13: R2.leg1, R3.Pin_0
  N14: J2.pin1, IC1.A_V-
  N15: J2.pin3, IC1.A_V+
  N16: J4.pin1, IC1.A_OUT, R6.wiper
  N17: J4.pin2, IC1.B_OUT, R5.wiper
  N18: IC1.A_-IN, R6.leg2, R8.Pin_0
  N19: IC1.B_-IN, R5.leg1, R7.Pin_1
